# Fritzing sketch semaphore (saved by Fritzing 0.9.0b)
circuit board: 8.46667cm x 5.64444cm
breadboards: 1

parts:
  XTAL1 = Crystal [frequency="16 MHz" package=THT]
  R1 = Resistor [tolerance=±5% resistance=68 package=THT]
  R2 = Resistor [tolerance=±5% resistance=220 package=THT]
  D1 = Rectifier Diode [part_number=1N4001 package="300 mil [THT]"]
  D2 = Rectifier Diode [part_number=1N4001 package="300 mil [THT]"]
  R3 = Resistor [tolerance=±5% resistance=68 package=THT]
  R4 = Resistor [tolerance=±5% resistance=1k package=THT]
  X1 = USB Connectors [package=usb-minib]
  AtTiny2313-20PU1 = IC, DIP package, 20 pins [chip_label=AtTiny2313-20PU spacing=300mil]
  J1 = Piezo Speaker
  LED1 = LEDs [package=led10mm]
  LED2 = LEDs [package=led10mm]
  LED3 = LEDs [package=led10mm]
  R5 = Resistor [tolerance=±5% resistance=68 package=THT]
  R6 = Resistor [tolerance=±5% resistance=68 package=THT]
  R7 = Resistor [tolerance=±5% resistance=68 package=THT]

nets:
  N1: XTAL1.pin_0, AtTiny2313-20PU1.pin4
  N2: XTAL1.pin_1, AtTiny2313-20PU1.pin5
  N3: R1.Pin_0, D1.cathode, X1.D+
  N4: R1.Pin_1, AtTiny2313-20PU1.pin6
  N5: R2.Pin_0, D2.cathode, R3.Pin_0, X1.D-
  N6: R2.Pin_1, R4.Pin_1, X1.VBUS, AtTiny2313-20PU1.pin20
  N7: D1.anode, D2.anode, X1.GND, AtTiny2313-20PU1.pin10, J1.pin2, LED1.C, LED2.C, LED3.C
  N8: R3.Pin_1, AtTiny2313-20PU1.pin7
  N9: R4.Pin_0, AtTiny2313-20PU1.pin1
  N10: AtTiny2313-20PU1.pin8, R7.Pin_0
  N11: AtTiny2313-20PU1.pin9, J1.pin1
  N12: AtTiny2313-20PU1.pin14, R5.Pin_0
  N13: AtTiny2313-20PU1.pin15, R6.Pin_0
  N14: LED1.A, R7.Pin_1
  N15: LED2.A, R5.Pin_1
  N16: LED3.A, R6.Pin_1
